// Logisim project lab10.circ as structural Verilog: 1 circuit, main circuit main
module main (
  input  R,
  input  S,
  input  S_2,
  input  R_2,
  input  Sn,
  input  Rn,
  input  D,
  input  J,
  input  K,
  input  J_2,
  input  K_2,
  input  in_12,
  input  in_13,
  input  in_14,
  input  in_15,
  output Q,
  output Q_2,
  output Q_prime,
  output Q_prime_2,
  output Q_3,
  output Q_prime_3,
  output Q_4,
  output Q_prime_4,
  output Q_5,
  output Q_prime_5,
  output out_26,
  output out_27
);

  wire clock_1_out, clock_2_out, clock_3_out, clock_4_out, clock_5_out, j_k_ff_1_q, j_k_ff_2_q, j_k_ff_3_q,
       j_k_ff_4_q, nand_1_out, nand_2_out, nand_3_out, nand_4_out, nand_7_out, nand_8_out, nand_9_out,
       nand_10_out, nand_15_out, nand_16_out, nand_17_out, nand_18_out, not_1_out, not_2_out, not_3_out,
       not_4_out, not_5_out, not_6_out;

  Clock clock_1 (.out(clock_1_out));
  Clock clock_2 (.out(clock_2_out));
  not not_1 (not_1_out, D);
  Clock clock_3 (.out(clock_3_out));
  Clock clock_4 (.out(clock_4_out));
  not not_2 (not_2_out, in_12);
  Clock clock_5 (.out(clock_5_out));
  nor nor_1 (Q, R, Q_prime);
  nor nor_2 (Q_prime, Q, S_2);
  nand nand_1 (nand_1_out, Sn, clock_1_out);
  nand nand_2 (nand_2_out, clock_1_out, Rn);
  nand nand_3 (nand_3_out, D, clock_2_out);
  nand nand_4 (nand_4_out, clock_2_out, not_1_out);
  not not_3 (not_3_out, in_13);
  J_K_Flip_Flop j_k_ff_1 (.J(in_12), .K(not_2_out), .Q(j_k_ff_1_q), .en(clock_5_out));  // open: clk, Qn, preset, reset
  nand nand_5 (Q_4, nand_3_out, Q_prime_4);
  nand nand_6 (Q_prime_4, Q_4, nand_4_out);
  nand nand_7 (nand_7_out, Q_prime_5, J, clock_3_out);
  nand nand_8 (nand_8_out, clock_3_out, K, Q_5);
  nand nand_9 (nand_9_out, out_26, J_2, clock_4_out);
  nand nand_10 (nand_10_out, clock_4_out, K_2, out_27);
  not not_4 (not_4_out, clock_4_out);
  J_K_Flip_Flop j_k_ff_2 (.J(in_13), .K(not_3_out), .Q(j_k_ff_2_q), .en(clock_5_out));  // open: clk, Qn, preset, reset
  nand nand_11 (Q_3, nand_1_out, Q_prime_3);
  nand nand_12 (Q_prime_3, Q_3, nand_2_out);
  nand nand_13 (Q_5, nand_7_out, Q_prime_5);
  nand nand_14 (Q_prime_5, Q_5, nand_8_out);
  not not_5 (not_5_out, in_14);
  nand nand_15 (nand_15_out, nand_9_out, nand_16_out);
  nand nand_16 (nand_16_out, nand_15_out, nand_10_out);
  not not_6 (not_6_out, in_15);
  J_K_Flip_Flop j_k_ff_3 (.J(in_14), .K(not_5_out), .Q(j_k_ff_3_q), .en(clock_5_out));  // open: clk, Qn, preset, reset
  J_K_Flip_Flop j_k_ff_4 (.J(in_15), .K(not_6_out), .Q(j_k_ff_4_q), .en(clock_5_out));  // open: clk, Qn, preset, reset
  nand nand_17 (nand_17_out, not_4_out, nand_15_out);
  nand nand_18 (nand_18_out, nand_16_out, not_4_out);
  nand nand_19 (Q_2, S, Q_prime_2);
  nand nand_20 (Q_prime_2, Q_2, R_2);
  nand nand_21 (out_26, nand_17_out, out_27);
  nand nand_22 (out_27, out_26, nand_18_out);

  // Notes on the sheet:
  //   Ex1)
  //   Ex2)
  //   Ex3)
  //   Truth Table
  //   Ex4) Master-Slave JK Flip Flop
  //   RS Flip Flop
  //   Synchronous RS FlipFlop
  //   Then draw truth table
  //   Draw logic circuit for JK Flip Flop
  //   JK Flip Flop
  //   Convert Circuit in Ex1 (synchronous RS Flip Flop) to a D-FlipFlop
  //   Output will change if the data inputs [J,K,Q,Q'] change while clock is high
  //   Ex5) Using JK Flip Flop (can use logisim block) build a four bit data register
  //   Need to make sure that Q and Q' do not assume thier new values until after trailing edge on the clock pulse
  //   RS Flip Flop
endmodule
