// Logisim project hw11.circ as structural Verilog: 1 circuit, main circuit main
module main (
  output Q3,
  output Q2,
  output Q1,
  output Q0
);

  wire and_1_out, and_2_out, clock_1_out;

  Clock clock_1 (.out(clock_1_out));
  J_K_Flip_Flop j_k_ff_1 (.J(1'b1), .clk(clock_1_out), .K(1'b1), .Q(Q0));  // open: Qn, preset, en, reset
  J_K_Flip_Flop j_k_ff_2 (.J(Q0), .clk(clock_1_out), .K(Q0), .Q(Q1));  // open: Qn, preset, en, reset
  and and_1 (and_1_out, Q1, Q0);
  J_K_Flip_Flop j_k_ff_3 (.J(and_1_out), .clk(clock_1_out), .K(and_1_out), .Q(Q2));  // open: Qn, preset, en, reset
  and and_2 (and_2_out, and_1_out, Q2);
  J_K_Flip_Flop j_k_ff_4 (.J(and_2_out), .clk(clock_1_out), .K(and_2_out), .Q(Q3));  // open: Qn, preset, en, reset

  // Notes on the sheet:
  //   4-Bit Synchronous Counter
  //   Output
endmodule
