// Logisim project lab11.circ as structural Verilog: 2 circuits, main circuit main
module main (
  input  in_1,
  input  in_2,
  input  in_3,
  input  in_4,
  input  in_5,
  input  in_6,
  input  in_7,
  input  in_8,
  input  in_9,
  input  in_10,
  input  in_11,
  input  in_12,
  input  in_13,
  input  in_14,
  input  in_15,
  input  in_16,
  input  in_17,
  input  in_18,
  input  in_19,
  output out_20,
  output out_21,
  output out_22,
  output out_23,
  output out_24,
  output out_25,
  output out_26,
  output out_27,
  output out_28,
  output out_29,
  output out_30,
  output Q0,
  output Q1,
  output Q2
);

  wire and_1_out, and_2_out, and_3_out, and_4_out, and_5_out, and_6_out, and_7_out, and_8_out, and_9_out,
       and_10_out, and_11_out, and_12_out, clock_1_out, clock_2_out, clock_3_out, clock_4_out, clock_5_out,
       clock_6_out, clock_7_out, clock_8_out, j_k_ff_2_qn, j_k_ff_3_q, j_k_ff_4_qn, j_k_ff_5_q, j_k_ff_5_qn,
       j_k_ff_6_q, j_k_ff_7_q, j_k_ff_8_qn, j_k_ff_10_qn, j_k_ff_11_qn, j_k_ff_12_q, j_k_ff_13_q,
       j_k_ff_14_q, j_k_ff_14_qn, j_k_ff_15_q, j_k_ff_16_qn, j_k_ff_18_qn, j_k_ff_19_qn, j_k_ff_20_q,
       j_k_ff_20_qn, j_k_ff_21_q, j_k_ff_22_q, j_k_ff_25_q, j_k_ff_26_q, j_k_ff_26_qn, j_k_ff_27_q,
       j_k_ff_28_q, not_1_out, not_2_out, not_3_out, not_4_out, not_5_out, not_6_out, not_7_out, not_8_out,
       not_9_out, not_10_out, not_11_out, or_1_out, or_2_out, or_3_out, or_4_out, or_5_out;

  Clock clock_1 (.out(clock_1_out));
  Clock clock_2 (.out(clock_2_out));
  not not_1 (not_1_out, in_1);
  Clock clock_3 (.out(clock_3_out));
  not not_2 (not_2_out, in_5);
  Clock clock_4 (.out(clock_4_out));
  not not_3 (not_3_out, in_7);
  and and_1 (and_1_out, in_6, not_3_out);
  not not_4 (not_4_out, or_1_out);
  Clock clock_5 (.out(clock_5_out));
  not not_5 (not_5_out, and_3_out);
  Clock clock_6 (.out(clock_6_out));
  Clock clock_7 (.out(clock_7_out));
  Clock clock_8 (.out(clock_8_out));
  not not_6 (not_6_out, in_2);
  J_K_Flip_Flop j_k_ff_1 (.J(in_1), .clk(clock_3_out), .K(not_1_out), .Q(out_20));  // open: Qn, preset, en, reset
  J_K_Flip_Flop j_k_ff_2 (
    .J(in_5), .clk(clock_4_out), .K(not_2_out), .Q(out_24), .Qn(j_k_ff_2_qn));  // open: preset, en, reset
  and and_2 (and_2_out, in_7, j_k_ff_13_q);
  or or_1 (or_1_out, and_1_out, and_2_out);
  J_K_Flip_Flop j_k_ff_3 (
    .J(or_1_out), .clk(clock_1_out), .K(not_4_out), .Q(j_k_ff_3_q));  // open: Qn, preset, en, reset
  J_K_Flip_Flop j_k_ff_4 (
    .J(j_k_ff_26_q), .clk(clock_5_out), .K(j_k_ff_26_qn), .Q(out_28), .Qn(j_k_ff_4_qn));  // open: preset, en, reset
  and and_3 (and_3_out, j_k_ff_20_qn, j_k_ff_14_qn, j_k_ff_5_qn);
  J_K_Flip_Flop j_k_ff_5 (
    .J(and_3_out), .clk(clock_6_out), .K(not_5_out), .Q(j_k_ff_5_q), .Qn(j_k_ff_5_qn));  // open: preset, en, reset
  J_K_Flip_Flop j_k_ff_6 (.J(1'b1), .clk(clock_7_out), .K(1'b1), .Q(j_k_ff_6_q));  // open: Qn, preset, en, reset
  J_K_Flip_Flop j_k_ff_7 (
    .J(1'b1), .clk(clock_8_out), .K(1'b1), .Q(j_k_ff_7_q), .reset(and_9_out));  // open: Qn, preset, en
  J_K_Flip_Flop j_k_ff_8 (.J(1'b1), .clk(clock_2_out), .K(1'b1), .Q(Q0), .Qn(j_k_ff_8_qn));  // open: preset, en, reset
  not not_7 (not_7_out, in_18);
  J_K_Flip_Flop j_k_ff_9 (.J(in_2), .clk(clock_3_out), .K(not_6_out), .Q(out_21));  // open: Qn, preset, en, reset
  J_K_Flip_Flop j_k_ff_10 (
    .J(out_24), .clk(clock_4_out), .K(j_k_ff_2_qn), .Q(out_25), .Qn(j_k_ff_10_qn));  // open: preset, en, reset
  and and_4 (and_4_out, j_k_ff_3_q, not_3_out);
  not not_8 (not_8_out, or_3_out);
  J_K_Flip_Flop j_k_ff_11 (
    .J(out_28), .clk(clock_5_out), .K(j_k_ff_4_qn), .Q(out_29), .Qn(j_k_ff_11_qn));  // open: preset, en, reset
  J_K_Flip_Flop j_k_ff_12 (
    .J(1'b1), .clk(j_k_ff_7_q), .K(1'b1), .Q(j_k_ff_12_q), .reset(and_9_out));  // open: Qn, preset, en
  buf and_5 (and_5_out, Q0);  // AND_Gate
  or or_2 (or_2_out, and_5_out, and_6_out);
  and and_6 (and_6_out, j_k_ff_8_qn, not_7_out);
  not not_9 (not_9_out, in_3);
  and and_7 (and_7_out, in_7, j_k_ff_25_q);
  or or_3 (or_3_out, and_4_out, and_7_out);
  J_K_Flip_Flop j_k_ff_13 (
    .J(or_3_out), .clk(clock_1_out), .K(not_8_out), .Q(j_k_ff_13_q));  // open: Qn, preset, en, reset
  J_K_Flip_Flop j_k_ff_14 (
    .J(j_k_ff_5_q), .clk(clock_6_out), .K(j_k_ff_5_qn), .Q(j_k_ff_14_q), .Qn(j_k_ff_14_qn));  // open: preset, en, reset
  J_K_Flip_Flop j_k_ff_15 (.J(1'b1), .clk(j_k_ff_6_q), .K(1'b1), .Q(j_k_ff_15_q));  // open: Qn, preset, en, reset
  J_K_Flip_Flop j_k_ff_16 (.J(1'b1), .clk(or_2_out), .K(1'b1), .Q(Q1), .Qn(j_k_ff_16_qn));  // open: preset, en, reset
  not not_10 (not_10_out, in_4);
  J_K_Flip_Flop j_k_ff_17 (.J(in_3), .clk(clock_3_out), .K(not_9_out), .Q(out_22));  // open: Qn, preset, en, reset
  J_K_Flip_Flop j_k_ff_18 (
    .J(out_25), .clk(clock_4_out), .K(j_k_ff_10_qn), .Q(out_26), .Qn(j_k_ff_18_qn));  // open: preset, en, reset
  and and_8 (and_8_out, j_k_ff_13_q, not_3_out);
  not not_11 (not_11_out, or_4_out);
  J_K_Flip_Flop j_k_ff_19 (
    .J(out_29), .clk(clock_5_out), .K(j_k_ff_11_qn), .Q(out_30), .Qn(j_k_ff_19_qn));  // open: preset, en, reset
  J_K_Flip_Flop j_k_ff_20 (
    .J(j_k_ff_14_q), .clk(clock_6_out), .K(j_k_ff_14_qn), .Q(j_k_ff_20_q), .Qn(j_k_ff_20_qn));  // open: preset, en, reset
  J_K_Flip_Flop j_k_ff_21 (.J(1'b1), .clk(j_k_ff_15_q), .K(1'b1), .Q(j_k_ff_21_q));  // open: Qn, preset, en, reset
  J_K_Flip_Flop j_k_ff_22 (
    .J(1'b1), .clk(j_k_ff_12_q), .K(1'b1), .Q(j_k_ff_22_q), .reset(and_9_out));  // open: Qn, preset, en
  and and_9 (and_9_out, j_k_ff_7_q, j_k_ff_12_q, j_k_ff_22_q);
  and and_10 (and_10_out, in_18, Q1);
  and and_11 (and_11_out, j_k_ff_16_qn, not_7_out);
  J_K_Flip_Flop j_k_ff_23 (.J(in_4), .clk(clock_3_out), .K(not_10_out), .Q(out_23));  // open: Qn, preset, en, reset
  J_K_Flip_Flop j_k_ff_24 (.J(out_26), .clk(clock_4_out), .K(j_k_ff_18_qn), .Q(out_27));  // open: Qn, preset, en, reset
  and and_12 (and_12_out, in_7, in_8);
  or or_4 (or_4_out, and_8_out, and_12_out);
  J_K_Flip_Flop j_k_ff_25 (
    .J(or_4_out), .clk(clock_1_out), .K(not_11_out), .Q(j_k_ff_25_q));  // open: Qn, preset, en, reset
  J_K_Flip_Flop j_k_ff_26 (
    .J(out_30), .clk(clock_5_out), .K(j_k_ff_19_qn), .Q(j_k_ff_26_q), .Qn(j_k_ff_26_qn));  // open: preset, en, reset
  or or_5 (or_5_out, and_10_out, and_11_out);
  J_K_Flip_Flop j_k_ff_27 (
    .J(j_k_ff_20_q), .clk(clock_6_out), .K(j_k_ff_20_qn), .Q(j_k_ff_27_q));  // open: Qn, preset, en, reset
  J_K_Flip_Flop j_k_ff_28 (.J(1'b1), .clk(j_k_ff_21_q), .K(1'b1), .Q(j_k_ff_28_q));  // open: Qn, preset, en, reset
  J_K_Flip_Flop j_k_ff_29 (.J(1'b1), .clk(or_5_out), .K(1'b1), .Q(Q2));  // open: Qn, preset, en, reset
  S_R_Flip_Flop s_r_ff_1 (.S(in_9), .clk(in_10), .R(in_11));  // open: Q, Qn, preset, reset, en
  J_K_Flip_Flop j_k_ff_30 (.J(in_12), .clk(in_13), .K(in_14));  // open: Q, Qn, preset, en, reset
  D_Flip_Flop d_ff_1 (.clk(in_15), .D(in_16));  // open: Q, Qn, preset, en, reset
  T_Flip_Flop t_ff_1 (.clk(in_17), .T(in_19));  // open: Q, Qn, preset, reset, en

  // Notes on the sheet:
  //   Ex1) 4 bit register
  //   Ex3-4)
  //   Build a binary counter
  //   Ex7) Build a base 7 counter
  //   Ex7) Base 8 up/down counter
  //   First flip flop -> MSB. Last flip flop -> LSB
  //   Ex5) Shift register with feedback. If the serial output of a shift register is connected to the input, sequence will circulate
  //   Ex6) N-bit ring counter, has n states, each of which contains all 0's except for a single 1
  //   Ex2) shfit register (4-bit) serial data input, transfer one bit at a time, a word of n-bits read into n flip flop shift register
endmodule

module _7seg (
  input  A,
  input  B,
  input  C,
  input  D,
  output a_2,
  output b_2,
  output c_2,
  output d_2,
  output e,
  output f,
  output g
);

  wire and_1_out, and_2_out, and_3_out, and_4_out, and_5_out, and_6_out, and_7_out, and_8_out, and_9_out,
       and_10_out, and_11_out, and_12_out, and_13_out, and_14_out, and_15_out, and_16_out, not_1_out,
       not_2_out, not_3_out, not_4_out, not_5_out, not_6_out, not_7_out, not_8_out, not_9_out, not_10_out,
       not_11_out, not_12_out, not_13_out, not_14_out, not_15_out, not_16_out, not_17_out, not_18_out,
       not_19_out, not_20_out, not_21_out;

  not not_1 (not_1_out, B);
  and and_1 (and_1_out, not_1_out, not_2_out);
  not not_2 (not_2_out, D);
  and and_2 (and_2_out, B, D);
  not not_3 (not_3_out, B);
  not not_4 (not_4_out, C);
  and and_3 (and_3_out, not_4_out, not_5_out);
  not not_5 (not_5_out, D);
  and and_4 (and_4_out, C, D);
  not not_6 (not_6_out, C);
  or or_1 (c_2, not_6_out, D, B);
  not not_7 (not_7_out, B);
  and and_5 (and_5_out, not_7_out, not_8_out);
  not not_8 (not_8_out, D);
  not not_9 (not_9_out, B);
  and and_6 (and_6_out, not_9_out, C);
  and and_7 (and_7_out, C, not_10_out);
  not not_10 (not_10_out, D);
  and and_8 (and_8_out, B, not_11_out, D);
  not not_11 (not_11_out, C);
  not not_12 (not_12_out, B);
  and and_9 (and_9_out, not_12_out, not_13_out);
  not not_13 (not_13_out, D);
  and and_10 (and_10_out, C, not_14_out);
  not not_14 (not_14_out, D);
  not not_15 (not_15_out, C);
  and and_11 (and_11_out, not_15_out, not_16_out);
  not not_16 (not_16_out, D);
  and and_12 (and_12_out, B, not_17_out);
  not not_17 (not_17_out, C);
  and and_13 (and_13_out, B, not_18_out);
  not not_18 (not_18_out, D);
  not not_19 (not_19_out, B);
  and and_14 (and_14_out, not_19_out, C);
  and and_15 (and_15_out, C, not_20_out);
  not not_20 (not_20_out, D);
  and and_16 (and_16_out, B, not_21_out);
  not not_21 (not_21_out, C);
  or or_2 (a_2, and_1_out, C, and_2_out, A);
  or or_3 (b_2, not_3_out, and_3_out, and_4_out);
  or or_4 (d_2, and_5_out, and_6_out, and_7_out, and_8_out, A);
  or or_5 (e, and_9_out, and_10_out);
  or or_6 (f, and_11_out, and_12_out, and_13_out, A);
  or or_7 (g, and_14_out, and_15_out, and_16_out, A);
endmodule
