// Logisim project hw12.circ as structural Verilog: 2 circuits, main circuit main
module main (
  input  in_1,
  input  in_2,
  input  in_3,
  input  in_4,
  input  in_5,
  input  in_6,
  input  in_7,
  input  in_8
);

  wire button_2_out, button_3_out, button_4_out, button_out;
  wire [3:0] calculator_1_out;

  Calculator calculator_1 (
    .F0(in_4), .F1(in_3), .F2(in_2), .F3(in_1), .L0(in_8), .L1(in_7), .L2(in_6), .L3(in_5),
    .OUT(calculator_1_out), .in_9(button_out), .in_10(button_2_out), .in_11(button_3_out),
    .in_12(button_4_out));
  Hex_Digit_Display hex_digit_display_1 (.value(calculator_1_out));  // open: dp
  Button button (.out(button_out));
  Button button_2 (.out(button_2_out));
  Button button_3 (.out(button_3_out));
  Button button_4 (.out(button_4_out));

  // Notes on the sheet:
  //   Ian's Cool Calculator
  //   (With Hexadecimal Support)
  //   Input 1
  //   Input 2
  //   How to use:
  //   Then press one of the operands to the right after inputting the BCD numbers
  //   Presto! Please note that inputs over 9 wil be represented with A-F (hexadecimal)
  //   Also note the left input is the first one, so if the left is 6, and right is 3, division will be 2
  //   If the right is 6 and left is 3, division will be zero as inputs are in wrong order
  //   If right is larger than left in subtraction, modular arithmetic (wrap around) is used
  //   First, input the BCD representations of the decimal numbers you want to input to the input locations
endmodule

module Calculator (
  input  F0,
  input  F1,
  input  F2,
  input  F3,
  input  L0,
  input  L1,
  input  L2,
  input  L3,
  input  in_9,
  input  in_10,
  input  in_11,
  input  in_12,
  output [3:0] OUT
);

  wire or_1_out, or_2_out, or_3_out, register_3_q, register_4_q, register_5_q;
  wire [3:0] adder_1_out, divider_1_out, multiplexer_1_out, multiplexer_2_out, multiplier_1_out,
       register_1_q, register_2_q, subtractor_1_out;

  Register #(.width(4)) register_1 (.D({F3, F2, F1, F0}), .en(1'b1), .Q(register_1_q), .clk(or_3_out));  // open: clr
  Register #(.width(4)) register_2 (.D({L3, L2, L1, L0}), .en(1'b1), .Q(register_2_q), .clk(or_3_out));  // open: clr
  Adder #(.width(4)) adder_1 (.a(register_1_q), .b(register_2_q), .out(adder_1_out));  // open: cin, cout
  Subtractor #(.width(4)) subtractor_1 (.a(register_1_q), .b(register_2_q), .out(subtractor_1_out));  // open: bin, bout
  or or_1 (or_1_out, in_9, in_10);
  or or_2 (or_2_out, in_11, in_12);
  Multiplier #(.width(4)) multiplier_1 (.a(register_1_q), .b(register_2_q), .out(multiplier_1_out));  // open: cin, cout
  Divider #(.width(4)) divider_1 (.a(register_1_q), .b(register_2_q), .out(divider_1_out));  // open: upper, rem
  Multiplexer #(.width(4), .enable("false")) multiplexer_1 (
    .in0(divider_1_out), .in1(multiplier_1_out), .out(multiplexer_1_out), .sel(register_3_q));
  Multiplexer #(.width(4), .enable("false")) multiplexer_2 (
    .in0(subtractor_1_out), .in1(adder_1_out), .out(multiplexer_2_out), .sel(register_4_q));
  or or_3 (or_3_out, or_1_out, or_2_out);
  Register #(.width(1)) register_3 (.D(in_10), .en(1'b1), .Q(register_3_q), .clk(or_1_out));  // open: clr
  Register #(.width(1)) register_4 (.D(in_12), .en(1'b1), .Q(register_4_q), .clk(or_2_out));  // open: clr
  Multiplexer #(.width(4), .enable("false")) multiplexer_3 (
    .in0(multiplexer_1_out), .in1(multiplexer_2_out), .out(OUT), .sel(register_5_q));
  Register #(.width(1)) register_5 (.D(or_2_out), .en(1'b1), .Q(register_5_q), .clk(or_3_out));  // open: clr

  // Notes on the sheet:
  //   Use input from any of the buttons as clock pulse for registers
  //   We need to choose which operation to use for the multiplexer
  //   So, we have these registers that hold the button press
  //   division/mulitplication
  //   addition/subtraction
  //   This one to choose whether to take input from */ or +- registers
endmodule
