// Logisim project compare4.circ as structural Verilog: 2 circuits, main circuit main
module main (
  input  A3,
  input  A2,
  input  A1,
  input  A0,
  input  B3,
  input  B2,
  input  B1,
  input  B0,
  output out_9,
  output out_10
);

  wire compare2_1_e, compare2_1_l, compare2_2_e, compare2_2_l;

  compare2 compare2_1 (.A(A3), .B(A2), .C(B3), .D(B2), .L(compare2_1_l), .E(compare2_1_e));
  and and_1 (out_10, compare2_1_e, compare2_2_e);
  compare2 compare2_2 (.A(A1), .B(A0), .C(B1), .D(B0), .L(compare2_2_l), .E(compare2_2_e));
  or or_1 (out_9, compare2_1_l, compare2_2_l);

  // Notes on the sheet:
  //   output for greater than will be true if B > A, output for equal to will be true if B = A
  //   output for compare greater than
  //   output for compare equal to
endmodule

module compare2 (
  input  A,
  input  B,
  input  C,
  input  D,
  output L,
  output E
);

  wire and_1_out, and_2_out, and_3_out, and_4_out, and_5_out, and_6_out, and_7_out, not_1_out, not_2_out,
       not_3_out, not_4_out, not_5_out, not_6_out, not_7_out, not_8_out, not_9_out, not_10_out, not_11_out,
       not_12_out;

  not not_1 (not_1_out, A);
  not not_2 (not_2_out, B);
  and and_1 (and_1_out, not_1_out, not_2_out, D);
  not not_3 (not_3_out, A);
  and and_2 (and_2_out, not_3_out, C);
  not not_4 (not_4_out, B);
  and and_3 (and_3_out, not_4_out, C, D);
  not not_5 (not_5_out, A);
  not not_6 (not_6_out, B);
  not not_7 (not_7_out, C);
  not not_8 (not_8_out, D);
  not not_9 (not_9_out, A);
  not not_10 (not_10_out, C);
  not not_11 (not_11_out, B);
  not not_12 (not_12_out, D);
  or or_1 (L, and_1_out, and_2_out, and_3_out);
  and and_4 (and_4_out, not_5_out, not_6_out, not_7_out, not_8_out);
  and and_5 (and_5_out, not_9_out, B, not_10_out, D);
  and and_6 (and_6_out, A, not_11_out, C, not_12_out);
  and and_7 (and_7_out, A, B, C, D);
  or or_2 (E, and_4_out, and_5_out, and_6_out, and_7_out);
endmodule
