// Logisim project lab7_1.circ as structural Verilog: 1 circuit, main circuit main
module main (
  input  lab7_1,
  input  in_2
);

  wire and_1_out, and_2_out, not_1_out, not_2_out, or_1_out;

  not not_1 (not_1_out, lab7_1);
  not not_2 (not_2_out, in_2);
  and and_1 (and_1_out, not_1_out, in_2);
  and and_2 (and_2_out, lab7_1, not_2_out);
  or or_1 (or_1_out, and_1_out, and_1_out, and_1_out, and_2_out, and_2_out);
endmodule
