// Logisim project lab7_2.circ as structural Verilog: 1 circuit, main circuit main
module main (
  input  NAND,
  input  in_2,
  input  XOR,
  input  in_4,
  input  in_5,
  input  in_6,
  input  in_7,
  input  in_8
);

  wire and_1_out, and_2_out, and_3_out, and_4_out, and_5_out, not_1_out, not_2_out, not_3_out, not_4_out,
       not_5_out, not_6_out, not_7_out, or_1_out, or_2_out, or_3_out;

  and and_1 (and_1_out, NAND, in_2);
  not not_1 (not_1_out, XOR);
  not not_2 (not_2_out, in_4);
  or or_1 (or_1_out, in_5, in_6);
  not not_3 (not_3_out, in_7);
  not not_4 (not_4_out, in_8);
  not not_5 (not_5_out, and_1_out);
  and and_2 (and_2_out, not_1_out, in_4);
  and and_3 (and_3_out, XOR, not_2_out);
  not not_6 (not_6_out, or_1_out);
  and and_4 (and_4_out, not_3_out, in_8);
  and and_5 (and_5_out, in_7, not_4_out);
  or or_2 (or_2_out, and_2_out, and_2_out, and_2_out, and_3_out, and_3_out);
  or or_3 (or_3_out, and_4_out, and_4_out, and_4_out, and_5_out, and_5_out);
  not not_7 (not_7_out, or_3_out);

  // Notes on the sheet:
  //   NOR
  //   XNOR
endmodule
