// Logisim project lab7_4.circ as structural Verilog: 1 circuit, main circuit main
module main (
  input  in_1,
  input  in_2,
  input  in_3,
  input  in_4,
  output out_5
);

  wire and_1_out, nand_1_out, nand_2_out, nor_1_out, or_1_out, xor_1_out;

  nand nand_1 (nand_1_out, in_1, in_2);
  nand nand_2 (nand_2_out, in_1, in_4);
  nor nor_1 (nor_1_out, in_2, in_3);
  and and_1 (and_1_out, nand_1_out, in_2);
  or or_1 (or_1_out, in_3, nand_2_out);
  xor xor_1 (xor_1_out, and_1_out, nor_1_out);
  nand nand_3 (out_5, xor_1_out, or_1_out);
endmodule
