// Logisim project lab7_5.circ as structural Verilog: 1 circuit, main circuit main
module main (
  input  in_1,
  input  original,
  input  in_3,
  input  a,
  input  b,
  input  c,
  output out_7,
  output x
);

  wire and_1_out, and_2_out, and_3_out, nand_1_out, not_1_out, not_2_out, not_3_out, not_4_out, not_5_out,
       not_6_out, or_2_out, xnor_1_out;

  not not_1 (not_1_out, in_1);
  not not_2 (not_2_out, original);
  not not_3 (not_3_out, a);
  not not_4 (not_4_out, b);
  not not_5 (not_5_out, c);
  and and_1 (and_1_out, not_3_out, not_4_out);
  and and_2 (and_2_out, b, not_5_out);
  and and_3 (and_3_out, not_1_out, original);
  xnor xnor_1 (xnor_1_out, not_2_out, in_3);
  not not_6 (not_6_out, in_3);
  or or_1 (x, and_1_out, and_2_out);
  or or_2 (or_2_out, in_1, and_3_out);
  nand nand_1 (nand_1_out, xnor_1_out, not_6_out);
  xor xor_1 (out_7, or_2_out, nand_1_out);

  // Notes on the sheet:
  //   simplified
endmodule
