// Logisim project excercise_1.circ as structural Verilog: 1 circuit, main circuit main
module main (
  input  in_1,
  input  in_2,
  input  in_3,
  input  in_4,
  input  in_5,
  input  [2:0] in_6,
  input  in_7,
  input  in_8,
  input  in_9,
  input  in_10,
  output out_11
);

  wire and_1_out, and_2_out, and_3_out, and_4_out, and_5_out, and_6_out, and_7_out, and_8_out,
       decoder_1_out0, decoder_1_out1, decoder_1_out2, decoder_1_out3, decoder_1_out4, decoder_1_out5,
       decoder_1_out6, decoder_1_out7;

  Decoder #(.select(3)) decoder_1 (
    .out0(decoder_1_out0), .out1(decoder_1_out1), .out2(decoder_1_out2), .out3(decoder_1_out3),
    .out4(decoder_1_out4), .out5(decoder_1_out5), .out6(decoder_1_out6), .out7(decoder_1_out7), .sel(in_6),
    .en(in_4));
  and and_1 (and_1_out, in_1, decoder_1_out0);
  and and_2 (and_2_out, in_2, decoder_1_out1);
  and and_3 (and_3_out, in_3, decoder_1_out2);
  and and_4 (and_4_out, in_5, decoder_1_out3);
  and and_5 (and_5_out, in_7, decoder_1_out4);
  and and_6 (and_6_out, in_8, decoder_1_out5);
  and and_7 (and_7_out, in_9, decoder_1_out6);
  and and_8 (and_8_out, in_10, decoder_1_out7);
  or or_1 (out_11, and_1_out, and_2_out, and_3_out, and_4_out, and_5_out, and_6_out, and_7_out, and_8_out);
endmodule
