// Logisim project excercise_2.circ as structural Verilog: 1 circuit, main circuit main
module main (
  input  in_1,
  input  in_2,
  input  in_3,
  input  in_4,
  input  [1:0] in_5,
  input  in_6,
  input  in_7,
  input  in_8,
  input  in_9,
  input  in_10,
  input  [2:0] in_11,
  input  [2:0] in_12,
  output out_13
);

  wire multiplexer_1_out, multiplexer_2_out;

  Multiplexer #(.select(2)) multiplexer_1 (
    .in0(in_1), .in1(in_2), .in2(in_3), .in3(in_4), .out(multiplexer_1_out), .sel(in_5));  // open: en
  Multiplexer #(.select(2)) multiplexer_2 (
    .in0(in_6), .in1(in_7), .in2(in_8), .in3(in_9), .out(multiplexer_2_out), .sel(in_5));  // open: en
  Multiplexer #(.enable("false")) multiplexer_3 (
    .in0(multiplexer_1_out), .in1(multiplexer_2_out), .out(out_13), .sel(in_10));
endmodule
