// Logisim project excercise_3.circ as structural Verilog: 1 circuit, main circuit main
module main (
  input  [2:0] in_1,
  input  [2:0] in_2,
  input  [2:0] in_3
);

  wire decoder_1_out0, decoder_1_out2, decoder_1_out7, decoder_2_out0, decoder_2_out2, decoder_2_out3,
       decoder_3_out0, decoder_3_out1, decoder_3_out5, or_1_out, or_2_out, or_3_out;

  Decoder #(.select(3)) decoder_1 (
    .out0(decoder_1_out0), .out2(decoder_1_out2), .out7(decoder_1_out7), .sel(in_1));  // open: out1, out3, out4, out5, out6, en
  Decoder #(.select(3)) decoder_2 (
    .out0(decoder_2_out0), .out2(decoder_2_out2), .out3(decoder_2_out3), .sel(in_2));  // open: out1, out4, out5, out6, out7, en
  Decoder #(.select(3)) decoder_3 (
    .out0(decoder_3_out0), .out1(decoder_3_out1), .out5(decoder_3_out5), .sel(in_3));  // open: out2, out3, out4, out6, out7, en
  or or_1 (or_1_out, decoder_1_out0, decoder_1_out2, decoder_1_out7);
  or or_2 (or_2_out, decoder_2_out0, decoder_2_out2, decoder_2_out3);
  or or_3 (or_3_out, decoder_3_out5, decoder_3_out1, decoder_3_out0);

  // Notes on the sheet:
  //   #3
  //   F1
  //   F2
  //   F3
endmodule
