// Logisim project excercise_4.circ as structural Verilog: 1 circuit, main circuit main
module main (
  input  [2:0] in_1,
  input  [2:0] in_2,
  input  [2:0] in_3,
  output out_4,
  output out_5,
  output out_6
);

  wire decoder_1_out0, decoder_1_out3, decoder_1_out4, decoder_2_out1, decoder_2_out2, decoder_2_out7,
       decoder_3_out1, decoder_3_out2, decoder_3_out7;

  Decoder #(.select(3), .enable("false")) decoder_1 (
    .out0(decoder_1_out0), .out3(decoder_1_out3), .out4(decoder_1_out4), .sel(in_1));  // open: out1, out2, out5, out6, out7
  Decoder #(.select(3), .enable("false")) decoder_2 (
    .out1(decoder_2_out1), .out2(decoder_2_out2), .out7(decoder_2_out7), .sel(in_2));  // open: out0, out3, out4, out5, out6
  Decoder #(.select(3), .enable("false")) decoder_3 (
    .out1(decoder_3_out1), .out2(decoder_3_out2), .out7(decoder_3_out7), .sel(in_3));  // open: out0, out3, out4, out5, out6
  or or_1 (out_4, decoder_1_out0, decoder_1_out3, decoder_1_out4);
  or or_2 (out_5, decoder_2_out1, decoder_2_out2, decoder_2_out7);
  or or_3 (out_6, decoder_3_out1, decoder_3_out2, decoder_3_out7);

  // Notes on the sheet:
  //   #4
  //   F1(A, B, C) = Em(0,3,4)
  //   F2(A, B, C) = Em(1,2,7)
  //   F3(A, B, C) = Em(1,2,7)
endmodule
