// Logisim project excercise_6.circ as structural Verilog: 1 circuit, main circuit main
module main (
  input  Leave_0,
  input  D,
  input  Leave_1,
  input  [2:0] ABC,
  output out_5
);

  wire not_1_out;

  not not_1 (not_1_out, D);
  Multiplexer #(.select(3), .enable("false")) multiplexer_1 (
    .in0(Leave_0), .in1(Leave_0), .in2(not_1_out), .in3(not_1_out), .in4(not_1_out), .in5(Leave_1),
    .in6(Leave_0), .in7(D), .out(out_5), .sel(ABC));
endmodule
