// Logisim project excercise__5.circ as structural Verilog: 1 circuit, main circuit main
module main (
  input  [3:0] in_1,
  output out_2
);

  wire decoder_1_out1, decoder_1_out3, decoder_1_out5, decoder_1_out9, decoder_1_out11, decoder_1_out12,
       decoder_1_out13, decoder_1_out14, decoder_1_out15;

  Decoder #(.select(4), .enable("false")) decoder_1 (
    .out1(decoder_1_out1), .out3(decoder_1_out3), .out5(decoder_1_out5), .out9(decoder_1_out9),
    .out11(decoder_1_out11), .out12(decoder_1_out12), .out13(decoder_1_out13), .out14(decoder_1_out14),
    .out15(decoder_1_out15), .sel(in_1));  // open: out0, out2, out4, out6, out7, out8, out10
  or or_1 (out_2, decoder_1_out1, decoder_1_out3, decoder_1_out5, decoder_1_out13, decoder_1_out15, decoder_1_out9, decoder_1_out11, decoder_1_out12, decoder_1_out14);
endmodule
