// Logisim project lab8.circ as structural Verilog: 4 circuits, main circuit main
module main (
  input  in_1,
  input  in_2,
  input  [1:0] in_3,
  input  _3_8_decoder,
  input  in_5,
  input  in_6,
  input  [2:0] in_7,
  input  in_8,
  input  in_9,
  input  in_10,
  input  in_11,
  input  [1:0] in_12,
  input  in_13,
  input  [2:0] in_14,
  input  [1:0] in_15,
  input  [2:0] in_16,
  input  [2:0] in_17,
  input  O1,
  input  in_19,
  input  in_20,
  input  Octal_inputs,
  input  in_22,
  input  in_23,
  input  O7,
  output out_25,
  output out_26,
  output out_27,
  output out_28,
  output out_29,
  output binary_outputs,
  output out_31,
  output out_32
);

  wire decoder2_4enable_1_d0, decoder2_4enable_1_d1, decoder2_4enable_1_d2, decoder2_4enable_1_d3,
       decoder_1_out0, decoder_1_out1, decoder_1_out2, decoder_1_out3, decoder_1_out4, decoder_1_out5,
       decoder_1_out6, decoder_1_out7, decoder_2_out0, decoder_2_out1, decoder_2_out2, decoder_2_out3,
       decoder_3_out0, decoder_3_out1, decoder_3_out2, decoder_3_out3, decoder_4_out0, decoder_4_out2,
       decoder_4_out3, decoder_4_out5, decoder_5_out0, decoder_5_out1, decoder_5_out2, decoder_5_out3,
       decoder_5_out4, decoder_5_out5, decoder_5_out6, decoder_5_out7, decoder_6_out0, decoder_6_out1,
       decoder_6_out2, decoder_6_out3, decoder_6_out4, decoder_6_out5, decoder_6_out6, decoder_6_out7,
       decoder_7_out0, decoder_7_out1, decoder_7_out2, decoder_7_out3, decoder_7_out4, decoder_7_out5,
       decoder_7_out6, decoder_7_out7, decoder_8_out0, decoder_8_out1, decoder_8_out2, decoder_8_out3,
       decoder_8_out4, decoder_8_out5, decoder_8_out6, decoder_8_out7, decoder_9_out0, decoder_9_out1,
       decoder_9_out2, decoder_9_out3, decoder_9_out4, decoder_9_out5, decoder_9_out6, decoder_9_out7,
       decoder_10_out0, decoder_10_out1, decoder_10_out2, decoder_10_out3, decoder_11_out0, decoder_11_out1,
       decoder_11_out2, decoder_11_out3, decoder_11_out4, decoder_11_out5, decoder_11_out6, decoder_11_out7,
       decoderusinggates3_8_1_d0, decoderusinggates3_8_1_d1, decoderusinggates3_8_1_d2,
       decoderusinggates3_8_1_d3, decoderusinggates3_8_1_d4, decoderusinggates3_8_1_d5,
       decoderusinggates3_8_1_d6, decoderusinggates3_8_1_d7, not_1_out, undriven;

  Decoder #(.select(3)) decoder_1 (
    .out0(decoder_1_out0), .out1(decoder_1_out1), .out2(decoder_1_out2), .out3(decoder_1_out3),
    .out4(decoder_1_out4), .out5(decoder_1_out5), .out6(decoder_1_out6), .out7(decoder_1_out7), .sel(in_14),
    .en(in_13));
  Decoder #(.select(2), .enable("false")) decoder_2 (
    .out0(decoder_2_out0), .out1(decoder_2_out1), .out2(decoder_2_out2), .out3(decoder_2_out3), .sel(in_15));
  DecoderUsingGates decoderusinggates_1 (.A(in_1), .B(in_2), .D0(out_25), .D1(out_26), .D2(out_27), .D3(out_28));
  DecoderUsingGates3_8 decoderusinggates3_8_1 (
    .A(_3_8_decoder), .B(in_5), .C(in_6), .D0(decoderusinggates3_8_1_d0), .D1(decoderusinggates3_8_1_d1),
    .D2(decoderusinggates3_8_1_d2), .D3(decoderusinggates3_8_1_d3), .D4(decoderusinggates3_8_1_d4),
    .D5(decoderusinggates3_8_1_d5), .D6(decoderusinggates3_8_1_d6), .D7(decoderusinggates3_8_1_d7));
  Decoder #(.select(2)) decoder_3 (
    .out0(decoder_3_out0), .out1(decoder_3_out1), .out2(decoder_3_out2), .out3(decoder_3_out3), .sel(in_12),
    .en(in_10));
  Decoder #(.select(3), .enable("false")) decoder_4 (
    .out0(decoder_4_out0), .out2(decoder_4_out2), .out3(decoder_4_out3), .out5(decoder_4_out5),
    .out6(decoder_4_out5), .sel(in_17));  // open: out1, out4, out7
  not not_1 (not_1_out, in_13);
  Decoder #(.select(3)) decoder_5 (
    .out0(decoder_5_out0), .out1(decoder_5_out1), .out2(decoder_5_out2), .out3(decoder_5_out3),
    .out4(decoder_5_out4), .out5(decoder_5_out5), .out6(decoder_5_out6), .out7(decoder_5_out7), .sel(in_14),
    .en(not_1_out));
  Decoder #(.select(3)) decoder_6 (
    .out0(decoder_6_out0), .out1(decoder_6_out1), .out2(decoder_6_out2), .out3(decoder_6_out3),
    .out4(decoder_6_out4), .out5(decoder_6_out5), .out6(decoder_6_out6), .out7(decoder_6_out7), .sel(in_16),
    .en(decoder_2_out0));
  Decoder #(.select(3)) decoder_7 (
    .out0(decoder_7_out0), .out1(decoder_7_out1), .out2(decoder_7_out2), .out3(decoder_7_out3),
    .out4(decoder_7_out4), .out5(decoder_7_out5), .out6(decoder_7_out6), .out7(decoder_7_out7), .sel(in_16),
    .en(decoder_2_out1));
  Decoder #(.select(3)) decoder_8 (
    .out0(decoder_8_out0), .out1(decoder_8_out1), .out2(decoder_8_out2), .out3(decoder_8_out3),
    .out4(decoder_8_out4), .out5(decoder_8_out5), .out6(decoder_8_out6), .out7(decoder_8_out7), .sel(in_16),
    .en(decoder_2_out2));
  Decoder #(.select(3)) decoder_9 (
    .out0(decoder_9_out0), .out1(decoder_9_out1), .out2(decoder_9_out2), .out3(decoder_9_out3),
    .out4(decoder_9_out4), .out5(decoder_9_out5), .out6(decoder_9_out6), .out7(decoder_9_out7), .sel(in_16),
    .en(decoder_2_out3));
  or or_1 (out_29, decoder_4_out0, decoder_4_out2, decoder_4_out3, decoder_4_out5);
  Decoder #(.select(2)) decoder_10 (
    .out0(decoder_10_out0), .out1(decoder_10_out1), .out2(decoder_10_out2), .out3(decoder_10_out3), .sel(in_3));  // open: en
  Decoder #(.select(3)) decoder_11 (
    .out0(decoder_11_out0), .out1(decoder_11_out1), .out2(decoder_11_out2), .out3(decoder_11_out3),
    .out4(decoder_11_out4), .out5(decoder_11_out5), .out6(decoder_11_out6), .out7(decoder_11_out7),
    .sel(in_7), .en(undriven));
  Decoder2_4Enable decoder2_4enable_1 (
    .A(in_8), .B(in_9), .C(in_11), .D0(decoder2_4enable_1_d0), .D1(decoder2_4enable_1_d1),
    .D2(decoder2_4enable_1_d2), .D3(decoder2_4enable_1_d3));
  or or_2 (binary_outputs, O7, in_23, in_22, Octal_inputs);
  or or_3 (out_31, O7, in_23, in_20, in_19);
  or or_4 (out_32, O7, in_22, in_20, O1);

  // Notes on the sheet:
  //   2-4 decoder
  //   4-16 decoder
  //   5-32 decoder
  //   Ex5) Build an octal to binary encoder
  //   Ex1) Build circuit using basic gates, works as decoder
  //   Ex2) 2-4 Decoder with enable (using block)
  //   Ex4) Design a circuit for the following logic function
  //   Ex3) Design 4-16 decoder using 3-8 decoders, then, 5-32 decoder
  //   F(x, y, z) = Em(0, 2, 3, 5)
  //   Enable (reversed, so 0 will enable, 1 will disable)
endmodule

module DecoderUsingGates (
  input  A,
  input  B,
  output D0,
  output D1,
  output D2,
  output D3
);

  wire not_1_out, not_2_out, not_3_out, not_4_out;

  not not_1 (not_1_out, A);
  not not_2 (not_2_out, B);
  not not_3 (not_3_out, A);
  not not_4 (not_4_out, B);
  and and_1 (D3, A, B);
  and and_2 (D0, not_1_out, not_2_out);
  and and_3 (D1, not_3_out, B);
  and and_4 (D2, A, not_4_out);

  // Notes on the sheet:
  //   Ex1) Build a circut using basic gates that works as a decoder
endmodule

module DecoderUsingGates3_8 (
  input  A,
  input  B,
  input  C,
  output D0,
  output D1,
  output D2,
  output D3,
  output D4,
  output D5,
  output D6,
  output D7
);

  wire not_1_out, not_2_out, not_3_out, not_4_out, not_5_out, not_6_out, not_7_out, not_8_out, not_9_out,
       not_10_out, not_11_out, not_12_out;

  not not_1 (not_1_out, A);
  not not_2 (not_2_out, B);
  not not_3 (not_3_out, C);
  not not_4 (not_4_out, A);
  not not_5 (not_5_out, B);
  not not_6 (not_6_out, A);
  not not_7 (not_7_out, C);
  not not_8 (not_8_out, A);
  not not_9 (not_9_out, B);
  not not_10 (not_10_out, C);
  not not_11 (not_11_out, B);
  not not_12 (not_12_out, C);
  and and_1 (D7, A, B, C);
  and and_2 (D0, not_1_out, not_2_out, not_3_out);
  and and_3 (D1, not_4_out, not_5_out, C);
  and and_4 (D2, not_6_out, B, not_7_out);
  and and_5 (D3, not_8_out, B, C);
  and and_6 (D4, A, not_9_out, not_10_out);
  and and_7 (D5, A, not_11_out, C);
  and and_8 (D6, A, B, not_12_out);
endmodule

module Decoder2_4Enable (
  input  A,
  input  B,
  input  C,
  output D0,
  output D1,
  output D2,
  output D3
);

  wire not_1_out, not_2_out, not_3_out, not_4_out, not_5_out, not_6_out;

  not not_1 (not_1_out, A);
  not not_2 (not_2_out, B);
  not not_3 (not_3_out, C);
  not not_4 (not_4_out, A);
  not not_5 (not_5_out, B);
  not not_6 (not_6_out, A);
  and and_1 (D3, A, B, C);
  and and_2 (D0, not_1_out, not_2_out, not_3_out);
  and and_3 (D1, not_4_out, not_5_out, C);
  and and_4 (D2, not_6_out, B, C);
endmodule
