// Logisim project 9comp.circ as structural Verilog: 1 circuit, main circuit main
module main (
  input  A0,
  input  B0,
  input  A1,
  input  B1,
  input  A2,
  input  B2,
  input  A3,
  input  B3,
  input  in_9,
  input  in_10,
  output Carry,
  output out_12,
  output out_13,
  output out_14,
  output out_15
);

  wire adder_1_cout, adder_1_out, adder_2_cout, adder_3_cout, adder_3_out, adder_4_cout, adder_5_cout,
       adder_5_out, adder_6_cout, adder_7_cout, adder_7_out, and_1_out, and_2_out, not_1_out, not_2_out,
       not_3_out, not_4_out, not_5_out, or_1_out;

  not not_1 (not_1_out, adder_1_out);
  Adder #(.width(1)) adder_1 (.a(B0), .b(A0), .out(adder_1_out), .cin(in_9), .cout(adder_1_cout));
  Adder #(.width(1)) adder_2 (.a(not_1_out), .b(1'b0), .out(out_12), .cin(in_10), .cout(adder_2_cout));
  not not_2 (not_2_out, adder_3_out);
  Adder #(.width(1)) adder_3 (.a(B1), .b(A1), .out(adder_3_out), .cin(adder_1_cout), .cout(adder_3_cout));
  not not_3 (not_3_out, adder_5_out);
  Adder #(.width(1)) adder_4 (.a(not_2_out), .b(or_1_out), .out(out_13), .cin(adder_2_cout), .cout(adder_4_cout));
  Adder #(.width(1)) adder_5 (.a(B2), .b(A2), .out(adder_5_out), .cin(adder_3_cout), .cout(adder_5_cout));
  Adder #(.width(1)) adder_6 (.a(not_3_out), .b(or_1_out), .out(out_14), .cin(adder_4_cout), .cout(adder_6_cout));
  not not_4 (not_4_out, adder_7_out);
  Adder #(.width(1)) adder_7 (.a(B3), .b(A3), .out(adder_7_out), .cin(adder_5_cout), .cout(adder_7_cout));
  Adder #(.width(1)) adder_8 (.a(not_4_out), .b(1'b0), .out(out_15), .cin(adder_6_cout), .cout(Carry));
  and and_1 (and_1_out, adder_5_out, adder_7_out);
  and and_2 (and_2_out, adder_3_out, adder_7_out);
  not not_5 (not_5_out, adder_7_cout);
  or or_1 (or_1_out, and_1_out, not_5_out, and_2_out);

  // Notes on the sheet:
  //   Output
endmodule
