// Logisim project 9comp2.circ as structural Verilog: 1 circuit, main circuit main
module main (
  input  in_1,
  input  in_2,
  input  in_3,
  input  in_4,
  input  in_5,
  output out_6,
  output out_7,
  output out_8,
  output out_9
);

  wire adder_1_cout, adder_2_cout, adder_3_cout;

  Adder #(.width(1)) adder_1 (.a(in_5), .out(out_6), .cin(in_1), .cout(adder_1_cout));  // open: b
  Adder #(.width(1)) adder_2 (.a(in_4), .out(out_7), .cin(adder_1_cout), .cout(adder_2_cout));  // open: b
  Adder #(.width(1)) adder_3 (.a(in_3), .out(out_8), .cin(adder_2_cout), .cout(adder_3_cout));  // open: b
  Adder #(.width(1)) adder_4 (.a(in_2), .out(out_9), .cin(adder_3_cout));  // open: b, cout
endmodule
