// Logisim project 9compfinal.circ as structural Verilog: 3 circuits, main circuit main
module main (
  input  in_1,
  input  A7___A4,
  input  in_3,
  input  in_4,
  input  in_5,
  input  in_6,
  input  in_7,
  input  in_8,
  input  in_9,
  input  in_10,
  input  in_11,
  input  in_12,
  input  in_13,
  input  in_14,
  input  in_15,
  input  in_16,
  input  in_17,
  output C0__ignore,
  output Sign__0___1,
  output out_20,
  output out_21,
  output out_22,
  output out_23,
  output out_24,
  output out_25,
  output out_26,
  output out_27
);

  wire n4_bitbcdadder_1_cn, n4_bitbcdadder_1_s0, n4_bitbcdadder_1_s1, n4_bitbcdadder_1_s2,
       n4_bitbcdadder_1_s3, n4_bitbcdadder_2_s0, n4_bitbcdadder_2_s1, n4_bitbcdadder_2_s2,
       n4_bitbcdadder_2_s3, n9s_comp_2_s0, n9s_comp_2_s1, n9s_comp_2_s2, n9s_comp_2_s3, n9s_comp_4_s0,
       n9s_comp_4_s1, n9s_comp_4_s2, n9s_comp_4_s3;

  not not_1 (Sign__0___1, n4_bitbcdadder_1_cn);
  _9S_COMP u_9s_comp_1 (
    .A0(n4_bitbcdadder_1_s0), .A1(n4_bitbcdadder_1_s1), .A2(n4_bitbcdadder_1_s2), .A3(n4_bitbcdadder_1_s3),
    .S0(out_23), .S1(out_22), .S2(out_21), .S3(out_20));
  _9S_COMP u_9s_comp_2 (
    .A0(in_8), .A1(in_7), .A2(in_6), .A3(in_5), .S0(n9s_comp_2_s0), .S1(n9s_comp_2_s1), .S2(n9s_comp_2_s2),
    .S3(n9s_comp_2_s3));
  _4_BITBCDADDER u_4_bitbcdadder_1 (
    .A3(in_1), .B3(n9s_comp_2_s3), .A2(A7___A4), .B2(n9s_comp_2_s2), .A1(in_3), .B1(n9s_comp_2_s1),
    .A0(in_4), .B0(n9s_comp_2_s0), .Cn(n4_bitbcdadder_1_cn), .S3(n4_bitbcdadder_1_s3),
    .S2(n4_bitbcdadder_1_s2), .S1(n4_bitbcdadder_1_s1), .S0(n4_bitbcdadder_1_s0), .Cn_1(in_17));
  _9S_COMP u_9s_comp_3 (
    .A0(n4_bitbcdadder_2_s0), .A1(n4_bitbcdadder_2_s1), .A2(n4_bitbcdadder_2_s2), .A3(n4_bitbcdadder_2_s3),
    .S0(out_27), .S1(out_26), .S2(out_25), .S3(out_24));
  _9S_COMP u_9s_comp_4 (
    .A0(in_16), .A1(in_15), .A2(in_14), .A3(in_13), .S0(n9s_comp_4_s0), .S1(n9s_comp_4_s1),
    .S2(n9s_comp_4_s2), .S3(n9s_comp_4_s3));
  _4_BITBCDADDER u_4_bitbcdadder_2 (
    .A3(in_9), .B3(n9s_comp_4_s3), .A2(in_10), .B2(n9s_comp_4_s2), .A1(in_11), .B1(n9s_comp_4_s1),
    .A0(in_12), .B0(n9s_comp_4_s0), .Cn(C0__ignore), .S3(n4_bitbcdadder_2_s3), .S2(n4_bitbcdadder_2_s2),
    .S1(n4_bitbcdadder_2_s1), .S0(n4_bitbcdadder_2_s0), .Cn_1(n4_bitbcdadder_1_cn));

  // Notes on the sheet:
  //   B7 - B4
  //   A3 - A0
  //   B3 - B0
endmodule

module _4_BITBCDADDER (
  input  A3,
  input  B3,
  input  A2,
  input  B2,
  input  A1,
  input  B1,
  input  A0,
  input  B0,
  input  Cn_1,
  output Cn,
  output S3,
  output S2,
  output S1,
  output S0
);

  wire adder_1_cout, adder_1_out, adder_3_cout, adder_3_out, adder_4_cout, adder_5_cout, adder_5_out,
       adder_6_cout, adder_7_cout, adder_7_out, adder_8_cout, and_1_out, and_2_out;

  or or_1 (Cn, adder_1_cout, and_1_out, and_2_out);
  and and_1 (and_1_out, adder_1_out, adder_3_out);
  and and_2 (and_2_out, adder_1_out, adder_5_out);
  Adder #(.width(1)) adder_1 (.a(B3), .b(A3), .out(adder_1_out), .cin(adder_3_cout), .cout(adder_1_cout));
  Adder #(.width(1)) adder_2 (.a(adder_1_out), .b(1'b0), .out(S3), .cin(adder_4_cout));  // open: cout
  Adder #(.width(1)) adder_3 (.a(B2), .b(A2), .out(adder_3_out), .cin(adder_5_cout), .cout(adder_3_cout));
  Adder #(.width(1)) adder_4 (.a(adder_3_out), .b(Cn), .out(S2), .cin(adder_6_cout), .cout(adder_4_cout));
  Adder #(.width(1)) adder_5 (.a(B1), .b(A1), .out(adder_5_out), .cin(adder_7_cout), .cout(adder_5_cout));
  Adder #(.width(1)) adder_6 (.a(adder_5_out), .b(Cn), .out(S1), .cin(adder_8_cout), .cout(adder_6_cout));
  Adder #(.width(1)) adder_7 (.a(B0), .b(A0), .out(adder_7_out), .cin(Cn_1), .cout(adder_7_cout));
  Adder #(.width(1)) adder_8 (.a(adder_7_out), .b(1'b0), .out(S0), .cin(1'b0), .cout(adder_8_cout));
endmodule

module _9S_COMP (
  input  A0,
  input  A1,
  input  A2,
  input  A3,
  output S0,
  output S1,
  output S2,
  output S3
);

  wire and_1_out, not_1_out, not_2_out, not_4_out;

  not not_1 (not_1_out, A0);
  not not_2 (not_2_out, A1);
  not not_3 (S3, A3);
  and and_1 (and_1_out, not_1_out, not_2_out);
  not not_4 (not_4_out, A2);
  and and_2 (S0, and_1_out, not_4_out);
  xor xor_1 (S1, A1, A2);

  assign S2 = A2;
endmodule
