// Logisim project lab9.circ as structural Verilog: 5 circuits, main circuit main
module main (
  input  Ex1,
  input  in_2,
  input  in_3,
  input  in_4,
  input  [1:0] in_5,
  input  in_6,
  input  X,
  input  Y,
  input  in_9,
  input  in_10,
  input  Z,
  input  Z_2,
  input  leave_1,
  input  leave_0,
  input  [1:0] XY,
  input  in_16,
  input  in_17,
  input  [1:0] in_18,
  input  [1:0] in_19,
  input  in_20,
  input  in_21,
  input  in_22,
  input  in_23,
  input  in_24,
  input  in_25,
  input  in_26,
  input  in_27,
  input  in_28,
  input  in_29,
  input  in_30,
  input  in_31,
  output out_32,
  output Z_3,
  output out_34,
  output out_35,
  output out_36,
  output out_37,
  output out_38,
  output out_39,
  output out_40,
  output out_41,
  output out_42,
  output out_43,
  output out_44
);

  wire and_1_out, and_2_out, and_3_out, and_4_out, and_5_out, and_6_out, and_7_out, decoder_1_out0,
       decoder_1_out1, decoder_1_out2, decoder_1_out3, demultiplexer_1_out0, demultiplexer_1_out1,
       demultiplexer_1_out2, demultiplexer_1_out3, fa_1_out_5, fa_2_out_5, fa_3_out_5, fa_4_out_5,
       ha_1_out_3, ha_1_out_4, ha_2_out_3, multiplexer_1_out, multiplexer_2_out, not_1_out, not_2_out,
       not_3_out, not_4_out, not_5_out;

  not not_1 (not_1_out, X);
  not not_2 (not_2_out, Z);
  not not_3 (not_3_out, Y);
  Decoder #(.select(2), .enable("false")) decoder_1 (
    .out0(decoder_1_out0), .out1(decoder_1_out1), .out2(decoder_1_out2), .out3(decoder_1_out3), .sel(in_5));
  and and_1 (and_1_out, decoder_1_out3, in_4);
  and and_2 (and_2_out, not_1_out, Y);
  and and_3 (and_3_out, Y, not_2_out);
  and and_4 (and_4_out, X, not_3_out, Z);
  not not_4 (not_4_out, Z_2);
  Decoder #(.select(2)) decoder_2 (.out0(out_34), .out1(out_35), .out2(out_36), .out3(out_37), .sel(in_19), .en(in_17));
  HA ha_1 (.in_1(in_20), .in_2(in_21), .out_3(ha_1_out_3), .out_4(ha_1_out_4));
  FA fa_1 (.in_1(in_23), .in_2(in_24), .in_3(in_31), .out_4(out_41), .out_5(fa_1_out_5));
  and and_5 (and_5_out, decoder_1_out2, in_3);
  and and_6 (and_6_out, decoder_1_out1, in_2);
  or or_1 (out_32, and_1_out, and_5_out, and_6_out, and_7_out);
  or or_2 (Z_3, and_2_out, and_3_out, and_4_out);
  HA ha_2 (.in_1(ha_1_out_4), .in_2(in_22), .out_3(ha_2_out_3), .out_4(out_39));
  FA fa_2 (.in_1(in_25), .in_2(in_26), .in_3(fa_1_out_5), .out_4(out_42), .out_5(fa_2_out_5));
  and and_7 (and_7_out, decoder_1_out0, Ex1);
  Multiplexer #(.select(2), .enable("false")) multiplexer_1 (
    .in0(Z_2), .in1(not_4_out), .in2(leave_1), .in3(leave_0), .out(multiplexer_1_out), .sel(XY));
  or or_3 (out_38, ha_1_out_3, ha_2_out_3);
  FA fa_3 (.in_1(in_27), .in_2(in_28), .in_3(fa_2_out_5), .out_4(out_43), .out_5(fa_3_out_5));
  Multiplexer #(.enable("false")) multiplexer_2 (.in0(in_6), .in1(in_9), .out(multiplexer_2_out), .sel(not_5_out));
  not not_5 (not_5_out, in_10);
  FA fa_4 (.in_1(in_29), .in_2(in_30), .in_3(fa_3_out_5), .out_4(out_44), .out_5(fa_4_out_5));
  Demultiplexer #(.select(2), .enable("false")) demultiplexer_1 (
    .out0(demultiplexer_1_out0), .out1(demultiplexer_1_out1), .out2(demultiplexer_1_out2),
    .out3(demultiplexer_1_out3), .in(in_16), .sel(in_18));
  xor xor_1 (out_40, fa_4_out_5, out_44);

  // Notes on the sheet:
  //   Ex4)
  //   -Output is 0 regardless of z
  //   -Output is 1 regardless of z
  //   Ex5) 1-4 DEMUX using Decoder
  //   Ex7) Build 4-bit parallel adder
  //   4-1 MUX using one decoder
  //   Ex2) xyz -> 4-1 MUX and an inverter
  //   Behavior attempting to mimick
  //   Implement truth table with 4-1 MUX
  //   Ex6) Bulid Full adder from Half adder
  //   -Output is z
  //   -Output is z'
  //   Using Decoder
  //   Connect x and y to the control input. For each combination value of x and y one of the following apply
  //   Behavior using MUX
  //   Behavior of regular DMX
endmodule

module ex4test (
  input  X,
  input  Y,
  input  Z,
  output R
);

  wire and_1_out, and_2_out, and_3_out, and_4_out, not_1_out, not_2_out, not_3_out, not_4_out, not_5_out,
       not_6_out;

  not not_1 (not_1_out, X);
  not not_2 (not_2_out, Y);
  not not_3 (not_3_out, X);
  not not_4 (not_4_out, Z);
  not not_5 (not_5_out, Y);
  not not_6 (not_6_out, Z);
  and and_1 (and_1_out, not_1_out, not_2_out, Z);
  and and_2 (and_2_out, not_3_out, Y, not_4_out);
  and and_3 (and_3_out, X, not_5_out, not_6_out);
  and and_4 (and_4_out, X, Y, Z);
  or or_1 (R, and_1_out, and_2_out, and_3_out, and_4_out);
endmodule

module HA (
  input  in_1,
  input  in_2,
  output out_3,
  output out_4
);

  xor xor_1 (out_3, in_1, in_2);
  and and_1 (out_4, in_1, in_2);
endmodule

module FA (
  input  in_1,
  input  in_2,
  input  in_3,
  output out_4,
  output out_5
);

  wire ha_1_out_3, ha_1_out_4, ha_2_out_3;

  HA ha_1 (.in_1(in_1), .in_2(in_2), .out_3(ha_1_out_3), .out_4(ha_1_out_4));
  HA ha_2 (.in_1(ha_1_out_4), .in_2(in_3), .out_3(ha_2_out_3), .out_4(out_5));
  or or_1 (out_4, ha_1_out_3, ha_2_out_3);
endmodule

module Ex2 (
  input  X,
  input  Y,
  input  Z,
  output Z_2
);

  wire and_1_out, and_2_out, and_3_out, not_1_out, not_2_out, not_3_out;

  not not_1 (not_1_out, X);
  not not_2 (not_2_out, Z);
  not not_3 (not_3_out, Y);
  and and_1 (and_1_out, not_1_out, Y);
  and and_2 (and_2_out, Y, not_2_out);
  and and_3 (and_3_out, X, not_3_out, Z);
  or or_1 (Z_2, and_1_out, and_2_out, and_3_out);
endmodule
